# Fritzing sketch fio shield (saved by Fritzing 0.9.1b)
stripboards: 1

parts:
  Part1 = NCP1402 Step-Up Breakout [part_number=NCP1402]
  3-Axis_Accelerometer1 = 3-Axis Accelerometer Breakout - MMA8452Q
  R1 = Resistor [tolerance=±5% resistance=33k package=THT]
  R2 = Resistor [tolerance=±5% resistance=18k package=THT]
  U1 = ENCODER-QUADRATURE [package=encoder-16mm-quad]

nets:
  GND: Part1.GND, 3-Axis_Accelerometer1.GND, R1.Pin_0, U1.A_-_gnd
  N1: Part1.VOUT, U1.B_-_5v
  VIN: Part1.VIN, 3-Axis_Accelerometer1.3.3V
  N2: R1.Pin_1, R2.Pin_0
  N3: R2.Pin_1, U1.C_-_output

notes:
  3v3
  gnd
  D10
  A5
  A4

custom parts:
  NCP1402 Step-Up Breakout: Description: The NCP1402 is a 5V DC-DC converter. The breakout board will accept voltage inputs between 1 and 4 Volts (such as 1 or 2 AA batteries) and output a constant, low ripple 5V output capable of sourcing up to 200 mA. This board is great for supplying power to 5V sensors or providing 5V from a a single AA battery. The breakout board includes the necessary peripheral components. The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
  ENCODER-QUADRATURE: quadrature encoder from Top-Up, part#EC16PHBF-B-20F-24-24C-16Y
