# Fritzing sketch 5V_to_3V3 (saved by Fritzing 0.9.1b)
breadboards: 1

parts:
  R1 = Resistor [tolerance=±5% resistance=18k package=THT]
  R2 = Resistor [tolerance=±5% resistance=33k package=THT]
  5V = DC Power [voltage=5]

nets:
  N1: R1.Pin_0, R2.Pin_1
  N2: R1.Pin_1, 5V.V+
  N3: R2.Pin_0, 5V.V-

notes:
  A
