# Fritzing sketch 5V_to_3V3_with_encoder (saved by Fritzing 0.9.1b)
breadboards: 1

parts:
  R1 = Resistor [tolerance=±5% resistance=18k package=THT]
  R2 = Resistor [tolerance=±5% resistance=33k package=THT]
  5V = DC Power [voltage=5]
  U1 = ENCODER-QUADRATURE [part_number="MA3 Shaft Encoder" package=encoder-16mm-quad]

nets:
  N1: R1.Pin_0, R2.Pin_1
  N2: R1.Pin_1, U1.C
  N3: R2.Pin_0, 5V.V-, U1.A
  N4: 5V.V+, U1.B

notes:
  A
