# Fritzing sketch 5V_to_3V3_with_encoder_and_stepup (saved by Fritzing 0.9.1b)
breadboards: 1

parts:
  R1 = Resistor [tolerance=±5% resistance=18k package=THT]
  R2 = Resistor [tolerance=±5% resistance=33k package=THT]
  5V = DC Power [voltage=3.3V]
  U1 = ENCODER-QUADRATURE [part_number="MA3 Shaft Encoder" package=encoder-16mm-quad]
  Part1 = NCP1400 Step-Up Breakout [part_number=NCP1402]
  Part2 = Arduino Fio (Funnel I/O)
  3-Axis_Accelerometer1 = 3-Axis Accelerometer Breakout - MMA8452Q

nets:
  N1: R1.Pin_0, R2.Pin_1, Part2.D10_PWM/SS
  N2: R1.Pin_1, U1.C
  GND: R2.Pin_0, 5V.V-, U1.A, Part1.GND, Part2.GND, Part2.AREF
  N3: U1.B, Part1.VOUT
  VIN: Part1.VIN, Part2.VCC, Part2.D0/RXI
  N4: Part2.A4/SDA, 3-Axis_Accelerometer1.SDA
  N5: Part2.A5/SCL, 3-Axis_Accelerometer1.SCL

notes:
  A
